# Fritzing sketch CarWiring (saved by Fritzing 0.9.3b)

parts:
  Part1 = Arduino MKR1000
  3-pins_Hall_Effect_Sensor = mystery part, 3 pins [chip_label="Hall Effect Sensor"]
  LED1 = smd LED [color="White (4500K)" package="0603 [SMD]"]
  LED2 = smd LED [color="White (4500K)" package="0603 [SMD]"]
  R2 = Resistor [tolerance=±5% resistance=10k package="0402 [SMD]"]
  LED3 = smd LED [color="White (4500K)" package="0603 [SMD]"]
  U1 = DC-DC 2-24V Step Up Booster [package=THT]
  U2 = LIPO-1000mAh [package=lipo-1000]  # not connected
  R3 = Resistor [tolerance=±5% resistance=330 package="0402 [SMD]"]
  R4 = Resistor [tolerance=±5% resistance=330 package="0402 [SMD]"]
  R5 = Resistor [tolerance=±5% resistance=330 package="0402 [SMD]"]

nets:
  N1: Part1.D2_PWM, R4.Pin_1
  N2: Part1.D5_PWM, R5.Pin_1
  N3: Part1.D6, 3-pins_Hall_Effect_Sensor.pin3, R2.Pin_0, R3.Pin_1
  N4: Part1.GND, LED1.cathode, LED2.cathode, LED3.cathode, U1.pin4
  N5: Part1.VCC, R2.Pin_1, U1.pin3
  N6: 3-pins_Hall_Effect_Sensor.pin1, U1.pin1
  N7: 3-pins_Hall_Effect_Sensor.pin2, U1.pin2
  N8: LED1.anode, R5.Pin_0
  N9: LED2.anode, R4.Pin_0
  N10: LED3.anode, R3.Pin_0

custom parts:
  Arduino MKR1000: MKR1000 is a powerful board that combines the functionality of the Zero and the Wi-Fi Shield. It is the ideal solution for makers wanting to design IoT projects with minimal previous experience in networking
  DC-DC 2-24V Step Up Booster: Convertisseur DC-DC 2-24V 2A
